# Fritzing sketch L298N (saved by Fritzing 0.9.4)

parts:
  L298N1 = L298N DC motor driver
  M1 = DC Motor
  Part1 = Arduino Uno (Rev3)
  VCC1 = Battery

nets:
  N1: L298N1.OUT3, M1.pin_2
  N2: L298N1.OUT4, M1.pin_1
  GND: L298N1.GND, Part1.GND, VCC1.-
  5V: L298N1.5V, Part1.5V
  N3: L298N1.ENA, Part1.D9_PWM
  N4: L298N1.IN1, Part1.D3_PWM
  N5: L298N1.IN2, Part1.D2

custom parts:
  L298N DC motor driver: 2x DC motor driver with 78M05 positive voltage regulator (7..35 V) L298N: max 46 V, 2 A Set 5 V Enable jumper to enable 5 V regultor (needed for the L298N) and +5 V output at screw terminal or supply external +5 V at screw terminal Set ENA and/or ENB to +5 V to enable motor permanently or supply ENA and/or ENB with PWM signal IN1 and IN2 set rotation directory for motor A (OUT1/OUT2) IN2 and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
