# Fritzing sketch BasicLightSensor (saved by Fritzing 0.9.4)
breadboards: 1

parts:
  Part1 = Arduino Uno (Rev3)
  e-radionica_com1 = LM393 LDR breakout [part_number=100027]
  LED1 = LED - 5mm [color="Red (633nm)" package="5 mm [THT]"]  # not connected
  LED2 = LED - 5mm [color="Red (633nm)" package="5 mm [THT]"]  # not connected
  R1 = Resistor [tolerance=±5% resistance=220 package=THT]
  R2 = Resistor [tolerance=±5% resistance=220 package=THT]  # not connected

nets:
  N1: Part1.A5/SCL, e-radionica_com1.AO
  5V: Part1.5V, e-radionica_com1.VCC
  GND: Part1.GND, e-radionica_com1.GND, R1.Pin_1
