# Fritzing sketch UltraLCD_mill (saved by Fritzing 0.9.4)
breadboards: 1

parts:
  Part1 = Arduino Uno (Rev3)
  HC-SR04_Sensor_1 = HC-SR04 Ultrasonic Distance Sensor
  Part2 = LCD1602-I2C
  LED1 = LED - 5mm [color="Red (633nm)" package="5 mm [THT]"]  # not connected
  LED2 = LED - 5mm [color="Red (633nm)" package="5 mm [THT]"]  # not connected
  R1 = Resistor [tolerance=±5% resistance=220 package=THT]  # not connected
  R2 = Resistor [tolerance=±5% resistance=220 package=THT]  # not connected
  buz1 = Piezo Buzzer  # not connected

nets:
  N1: Part1.D12/MISO, HC-SR04_Sensor_1.ECHO
  N2: Part1.D13/SCK, HC-SR04_Sensor_1.TRIG
  GND: Part1.GND, HC-SR04_Sensor_1.GND, Part2.GND
  N3: Part1.A4/SDA, Part2.SDA
  N4: Part1.A5/SCL, Part2.SCL
  VCC: Part1.5V, HC-SR04_Sensor_1.VCC, Part2.VCC

custom parts:
  LCD1602-I2C: A standard character display, usually with 2x16 characters. Comes in many colors with LCM1602 IIC attached.
  Piezo Buzzer: Part from https://www.nutsvolts.com/magazine/article/november2012_SmileysWorkshop modified to be .3 in spacing to match the adafruit buzzer 5V breadboard friendly part.
